// Logisim project trab1.circ as structural Verilog: 11 circuits, main circuit ULA
module main (
  input  [3:0] in_1,
  input  [3:0] in_2,
  input  [1:0] in_3
);

  wire ula_1_f, ula_1_z;
  wire [3:0] ula_1_r0;

  ULA ula_1 (
    .A0(in_1[0]), .A1(in_1[1]), .A2(in_1[2]), .A3(in_1[3]), .B0(in_2[0]), .B1(in_2[1]), .B2(in_2[2]),
    .B3(in_2[3]), .S1(in_3[1]), .S0(in_3[0]), .F(ula_1_f), .R0(ula_1_r0[0]), .R1(ula_1_r0[1]),
    .R2(ula_1_r0[2]), .R3(ula_1_r0[3]), .Z(ula_1_z));
  // Probe on ula_1_f
  // Probe on ula_1_z
  // Probe on ula_1_r0

  // Notes on the sheet:
  //   Teste A
  //   Teste B
  //   Teste Seletor
  //   NAO MODIFIQUE ESTE CIRCUITO NEM OS FIOS DE TESTE
  //   Saida F
  //   Saida Z
  //   Saida R
endmodule

module ULA (
  input  A0,
  input  A1,
  input  A2,
  input  A3,
  input  B0,
  input  B1,
  input  B2,
  input  B3,
  input  S1,
  input  S0,
  output R0,
  output R1,
  output R2,
  output R3,
  output F,
  output Z
);

  wire shift_left_1_r0, shift_left_1_r1, shift_left_1_r2, shift_left_1_r3, shift_right_1_r0,
       shift_right_1_r1, shift_right_1_r2, shift_right_1_r3, somador_1_overflow, somador_1_r0, somador_1_r1,
       somador_1_r2, somador_1_r3, subtrator_1_overflow, subtrator_1_r0, subtrator_1_r1, subtrator_1_r2,
       subtrator_1_r3;

  somador somador_1 (
    .B3(B3), .A3(A3), .B2(B2), .A2(A2), .B1(B1), .A1(A1), .B0(B0), .A0(A0), .R3(somador_1_r3),
    .R2(somador_1_r2), .R1(somador_1_r1), .R0(somador_1_r0), .overflow(somador_1_overflow));
  subtrator subtrator_1 (
    .B3(B3), .A3(A3), .B2(B2), .A2(A2), .B1(B1), .A1(A1), .B0(B0), .A0(A0), .R3(subtrator_1_r3),
    .R2(subtrator_1_r2), .R1(subtrator_1_r1), .R0(subtrator_1_r0), .overflow(subtrator_1_overflow));
  shift_left shift_left_1 (
    .B1(B1), .B2(B2), .B3(B3), .B0(B0), .A3(A3), .A2(A2), .A1(A1), .A0(A0), .R3(shift_left_1_r3),
    .R2(shift_left_1_r2), .R1(shift_left_1_r1), .R0(shift_left_1_r0));
  shift_right shift_right_1 (
    .B3(B3), .B2(B2), .B1(B1), .B0(B0), .A3(A3), .A2(A2), .A1(A1), .A0(A0), .R3(shift_right_1_r3),
    .R2(shift_right_1_r2), .R1(shift_right_1_r1), .R0(shift_right_1_r0));
  mux4 mux4_1 (
    .S1(S1), .S0(S0), .I0(somador_1_r0), .I1(subtrator_1_r0), .I2(shift_left_1_r0), .I3(shift_right_1_r0),
    .R(R0));
  mux4 mux4_2 (
    .S1(S1), .S0(S0), .I0(somador_1_r1), .I1(subtrator_1_r1), .I2(shift_left_1_r1), .I3(shift_right_1_r1),
    .R(R1));
  mux4 mux4_3 (
    .S1(S1), .S0(S0), .I0(somador_1_r2), .I1(subtrator_1_r2), .I2(shift_left_1_r2), .I3(shift_right_1_r2),
    .R(R2));
  mux4 mux4_4 (
    .S1(S1), .S0(S0), .I0(somador_1_r3), .I1(subtrator_1_r3), .I2(shift_left_1_r3), .I3(shift_right_1_r3),
    .R(R3));
  mux4 mux4_5 (.S1(S1), .S0(S0), .I0(somador_1_overflow), .I1(subtrator_1_overflow), .I2(1'b0), .I3(1'b0), .R(F));
  Zero zero_1 (.R0(R3), .R1(R2), .R2(R1), .R3(R0), .Z(Z));

  // Notes on the sheet:
  //   Este circuito deve ser modificado para implementar sua ULA
  //   Os fios estao apenas para teste, todos podem ser removidos
endmodule

module full_adder (
  input  A,
  input  B,
  input  Cin,
  output Cout,
  output R
);

  wire and_1_out, and_2_out, and_3_out, or_1_out, xor_1_out;

  xor xor_1 (xor_1_out, A, B);
  xor xor_2 (R, xor_1_out, Cin);
  and and_1 (and_1_out, A, Cin);
  and and_2 (and_2_out, A, B);
  and and_3 (and_3_out, B, Cin);
  or or_1 (or_1_out, and_1_out, and_2_out);
  or or_2 (Cout, or_1_out, and_3_out);
endmodule

module half_adder (
  input  A,
  input  B,
  output Cout,
  output R
);

  and and_1 (Cout, A, B);
  xor xor_1 (R, A, B);
endmodule

module somador (
  input  B3,
  input  A3,
  input  B2,
  input  A2,
  input  B1,
  input  A1,
  input  B0,
  input  A0,
  output R3,
  output R2,
  output R1,
  output R0,
  output overflow
);

  wire full_adder_1_cout, full_adder_2_cout, full_adder_3_cout, half_adder_1_cout, xor_1_out;

  xor xor_1 (xor_1_out, full_adder_1_cout, full_adder_2_cout);
  not not_1 (overflow, xor_1_out);
  full_adder full_adder_1 (.A(A3), .B(B3), .Cin(full_adder_2_cout), .Cout(full_adder_1_cout), .R(R3));
  full_adder full_adder_2 (.A(A2), .B(B2), .Cin(full_adder_3_cout), .Cout(full_adder_2_cout), .R(R2));
  full_adder full_adder_3 (.A(A1), .B(B1), .Cin(half_adder_1_cout), .Cout(full_adder_3_cout), .R(R1));
  half_adder half_adder_1 (.A(A0), .B(B0), .Cout(half_adder_1_cout), .R(R0));
endmodule

module subtrator (
  input  B3,
  input  A3,
  input  B2,
  input  A2,
  input  B1,
  input  A1,
  input  B0,
  input  A0,
  output R3,
  output R2,
  output R1,
  output R0,
  output overflow
);

  wire full_adder_1_cout, full_adder_2_cout, full_adder_3_cout, full_adder_4_cout, not_1_out, not_3_out,
       not_4_out, not_5_out, xor_1_out;

  not not_1 (not_1_out, B3);
  xor xor_1 (xor_1_out, full_adder_1_cout, full_adder_2_cout);
  not not_2 (overflow, xor_1_out);
  not not_3 (not_3_out, B2);
  full_adder full_adder_1 (.A(A3), .B(not_1_out), .Cin(full_adder_2_cout), .Cout(full_adder_1_cout), .R(R3));
  full_adder full_adder_2 (.A(A2), .B(not_3_out), .Cin(full_adder_3_cout), .Cout(full_adder_2_cout), .R(R2));
  not not_4 (not_4_out, B1);
  full_adder full_adder_3 (.A(A1), .B(not_4_out), .Cin(full_adder_4_cout), .Cout(full_adder_3_cout), .R(R1));
  not not_5 (not_5_out, B0);
  full_adder full_adder_4 (.A(A0), .B(not_5_out), .Cin(1'b1), .Cout(full_adder_4_cout), .R(R0));
endmodule

module mux4 (
  input  S1,
  input  S0,
  input  I0,
  input  I1,
  input  I2,
  input  I3,
  output R
);

  wire and_1_out, and_2_out, and_3_out, and_4_out, not_1_out, not_2_out, not_3_out, not_4_out;

  not not_1 (not_1_out, S1);
  not not_2 (not_2_out, S0);
  not not_3 (not_3_out, S1);
  not not_4 (not_4_out, S0);
  and and_1 (and_1_out, not_1_out, I0, not_2_out);
  and and_2 (and_2_out, I1, not_3_out, S0);
  and and_3 (and_3_out, S1, not_4_out, I2);
  and and_4 (and_4_out, S1, S0, I3);
  or or_1 (R, and_1_out, and_2_out, and_3_out, and_4_out);
endmodule

module shift_left (
  input  B1,
  input  B2,
  input  B3,
  input  B0,
  input  A3,
  input  A2,
  input  A1,
  input  A0,
  output R3,
  output R2,
  output R1,
  output R0
);

  wire mux2_1_s, mux2_2_s, mux2_3_s, mux2_4_s, mux2_5_s, mux2_6_s, mux2_7_s, mux2_8_s, mux2_9_s, mux2_10_s,
       mux2_11_s, mux2_12_s;

  mux2 mux2_1 (.B(B0), .I0(A3), .I1(A2), .S(mux2_1_s));
  mux2 mux2_2 (.B(B0), .I0(A2), .I1(A1), .S(mux2_2_s));
  mux2 mux2_3 (.B(B0), .I0(A1), .I1(A0), .S(mux2_3_s));
  mux2 mux2_4 (.B(B0), .I0(A0), .I1(1'b0), .S(mux2_4_s));
  mux2 mux2_5 (.B(B1), .I0(mux2_1_s), .I1(mux2_3_s), .S(mux2_5_s));
  mux2 mux2_6 (.B(B1), .I0(mux2_2_s), .I1(mux2_4_s), .S(mux2_6_s));
  mux2 mux2_7 (.B(B1), .I0(mux2_3_s), .I1(1'b0), .S(mux2_7_s));
  mux2 mux2_8 (.B(B1), .I0(mux2_4_s), .I1(1'b0), .S(mux2_8_s));
  mux2 mux2_9 (.B(B2), .I0(mux2_5_s), .I1(1'b0), .S(mux2_9_s));
  mux2 mux2_10 (.B(B2), .I0(mux2_6_s), .I1(1'b0), .S(mux2_10_s));
  mux2 mux2_11 (.B(B2), .I0(mux2_7_s), .I1(1'b0), .S(mux2_11_s));
  mux2 mux2_12 (.B(B2), .I0(mux2_8_s), .I1(1'b0), .S(mux2_12_s));
  mux2 mux2_13 (.B(B3), .I0(mux2_9_s), .I1(1'b0), .S(R3));
  mux2 mux2_14 (.B(B3), .I0(mux2_10_s), .I1(1'b0), .S(R2));
  mux2 mux2_15 (.B(B3), .I0(mux2_11_s), .I1(1'b0), .S(R1));
  mux2 mux2_16 (.B(B3), .I0(mux2_12_s), .I1(1'b0), .S(R0));
endmodule

module shift_right (
  input  B3,
  input  B2,
  input  B1,
  input  B0,
  input  A3,
  input  A2,
  input  A1,
  input  A0,
  output R3,
  output R2,
  output R1,
  output R0
);

  wire mux2_1_s, mux2_2_s, mux2_3_s, mux2_4_s, mux2_5_s, mux2_6_s, mux2_7_s, mux2_8_s, mux2_9_s, mux2_10_s,
       mux2_11_s, mux2_12_s;

  mux2 mux2_1 (.B(B0), .I0(A3), .I1(A3), .S(mux2_1_s));
  mux2 mux2_2 (.B(B0), .I0(A2), .I1(A3), .S(mux2_2_s));
  mux2 mux2_3 (.B(B0), .I0(A1), .I1(A2), .S(mux2_3_s));
  mux2 mux2_4 (.B(B0), .I0(A0), .I1(A1), .S(mux2_4_s));
  mux2 mux2_5 (.B(B1), .I0(mux2_1_s), .I1(mux2_1_s), .S(mux2_5_s));
  mux2 mux2_6 (.B(B1), .I0(mux2_2_s), .I1(mux2_1_s), .S(mux2_6_s));
  mux2 mux2_7 (.B(B1), .I0(mux2_3_s), .I1(mux2_1_s), .S(mux2_7_s));
  mux2 mux2_8 (.B(B1), .I0(mux2_4_s), .I1(mux2_2_s), .S(mux2_8_s));
  mux2 mux2_9 (.B(B2), .I0(mux2_5_s), .I1(mux2_5_s), .S(mux2_9_s));
  mux2 mux2_10 (.B(B2), .I0(mux2_6_s), .I1(mux2_5_s), .S(mux2_10_s));
  mux2 mux2_11 (.B(B2), .I0(mux2_7_s), .I1(mux2_5_s), .S(mux2_11_s));
  mux2 mux2_12 (.B(B2), .I0(mux2_8_s), .I1(mux2_5_s), .S(mux2_12_s));
  mux2 mux2_13 (.B(B3), .I0(mux2_9_s), .I1(mux2_9_s), .S(R3));
  mux2 mux2_14 (.B(B3), .I0(mux2_10_s), .I1(mux2_9_s), .S(R2));
  mux2 mux2_15 (.B(B3), .I0(mux2_11_s), .I1(mux2_9_s), .S(R1));
  mux2 mux2_16 (.B(B3), .I0(mux2_12_s), .I1(mux2_9_s), .S(R0));
endmodule

module mux2 (
  input  B,
  input  I0,
  input  I1,
  output S
);

  wire and_1_out, and_2_out, not_1_out;

  not not_1 (not_1_out, B);
  and and_1 (and_1_out, not_1_out, I0);
  and and_2 (and_2_out, B, I1);
  or or_1 (S, and_1_out, and_2_out);
endmodule

module Zero (
  input  R0,
  input  R1,
  input  R2,
  input  R3,
  output Z
);

  wire not_1_out, not_2_out, not_3_out, not_4_out;

  not not_1 (not_1_out, R0);
  not not_2 (not_2_out, R1);
  not not_3 (not_3_out, R2);
  not not_4 (not_4_out, R3);
  and and_1 (Z, not_1_out, not_2_out, not_3_out, not_4_out);
endmodule
